# Fritzing sketch Radiodan_app_simple (saved by Fritzing 0.8.3b)

parts:
  S2 = SWITCH-MOMENTARY-2 [package=tactile-pth]
  S1 = SWITCH-MOMENTARY-2 [package=tactile-pth]
  LED1 = RGB LED (com. cathode, rbg) [package="5 mm [THT]"]  # not connected
  R1 = Resistor [package="2010 [SMD]"]  # not connected
  RaspberryPi1 = Raspberry Pi Model B

nets:
  N1: S2.1, RaspberryPi1.#4
  N2: S1.1, RaspberryPi1.#21

custom parts:
  Raspberry Pi Model B: Raspberry Pi (Model B)
